# Fritzing sketch Arduino_Driver_Single (saved by Fritzing 1.0.2b)
breadboards: 1

parts:
  Part1 = Analog Digital MUX Breakout  # not connected
  Q1 = Basic FET P-Channel [package="TO220 [THT]"]
  Q2 = Basic FET P-Channel [package="TO220 [THT]"]
  Q3 = Basic FET P-Channel [package="TO220 [THT]"]
  Q4 = Basic FET P-Channel [package="TO220 [THT]"]
  Q5 = Basic FET P-Channel [package="TO220 [THT]"]
  Q6 = Basic FET P-Channel [package="TO220 [THT]"]
  Q7 = Basic FET P-Channel [package="TO220 [THT]"]
  Q8 = Basic FET P-Channel [package="TO220 [THT]"]
  Q14 = Basic FET P-Channel [package="TO220 [THT]"]
  Q15 = Basic FET P-Channel [package="TO220 [THT]"]
  Q16 = Basic FET P-Channel [package="TO220 [THT]"]
  Q17 = Basic FET P-Channel [package="TO220 [THT]"]
  Q18 = Basic FET P-Channel [package="TO220 [THT]"]
  Q19 = Basic FET P-Channel [package="TO220 [THT]"]
  Q20 = Basic FET P-Channel [package="TO220 [THT]"]
  Q21 = Basic FET P-Channel [package="TO220 [THT]"]
  R1 = Resistor [tolerance=±5% resistance=10k package="0402 [SMD]"]
  R2 = Resistor [tolerance=±5% resistance=10k package="0402 [SMD]"]
  R3 = Resistor [tolerance=±5% resistance=10k package="0402 [SMD]"]
  R4 = Resistor [tolerance=±5% resistance=10k package="0402 [SMD]"]
  R5 = Resistor [tolerance=±5% resistance=10k package="0402 [SMD]"]
  R6 = Resistor [tolerance=±5% resistance=10k package="0402 [SMD]"]
  R7 = Resistor [tolerance=±5% resistance=10k package="0402 [SMD]"]
  R8 = Resistor [tolerance=±5% resistance=10k package="0402 [SMD]"]
  R9 = Resistor [tolerance=±5% resistance=10k package="0402 [SMD]"]
  R10 = Resistor [tolerance=±5% resistance=10k package="0402 [SMD]"]
  R11 = Resistor [tolerance=±5% resistance=10k package="0402 [SMD]"]
  R12 = Resistor [tolerance=±5% resistance=10k package="0402 [SMD]"]
  R13 = Resistor [tolerance=±5% resistance=10k package="0402 [SMD]"]
  R14 = Resistor [tolerance=±5% resistance=10k package="0402 [SMD]"]
  R15 = Resistor [tolerance=±5% resistance=10k package="0402 [SMD]"]
  R16 = Resistor [tolerance=±5% resistance=10k package="0402 [SMD]"]
  Part2 = Arduino Uno (Rev3)
  J1 = Power Jack [package=power_jack_pth]
  J3 = female pin header, 8 pins [form="♀ (female)"]  # not connected
  J4 = female pin header, 8 pins [form="♀ (female)"]
  J5 = female pin header, 8 pins [form="♀ (female)"]  # not connected
  J6 = female pin header, 8 pins [form="♀ (female)"]
  J7 = female pin header, 8 pins [form="♀ (female)"]
  J8 = female pin header, 8 pins [form="♀ (female)"]

nets:
  N1: Q1.gate, R1.Pin_1
  N2: Q1.drain, J4.pin1
  N3: Q1.source, Q2.source, Q3.source, Q4.source, Q5.source, Q6.source, Q7.source, Q8.source, Q14.source, Q15.source, Q16.source, Q17.source, Q18.source, Q19.source, Q20.source, Q21.source, R1.Pin_0, R2.Pin_1, R3.Pin_0, R4.Pin_1, R5.Pin_0, R6.Pin_1, R7.Pin_0, R8.Pin_1, R9.Pin_0, R10.Pin_1, R11.Pin_0, R12.Pin_1, R13.Pin_0, R14.Pin_1, R15.Pin_0, R16.Pin_1, J1.PWR
  N4: Q2.gate, R3.Pin_1
  N5: Q2.drain, J4.pin2
  N6: Q3.gate, R5.Pin_1
  N7: Q3.drain, J4.pin3
  N8: Q4.gate, R7.Pin_1
  N9: Q4.drain, J4.pin4
  N10: Q5.gate, R11.Pin_1
  N11: Q5.drain, J4.pin6
  N12: Q6.gate, R13.Pin_1
  N13: Q6.drain, J4.pin7
  N14: Q7.gate, R9.Pin_1
  N15: Q7.drain, J4.pin5
  N16: Q8.gate, R15.Pin_1
  N17: Q8.drain, J4.pin8
  N18: Q14.gate, R2.Pin_0
  N19: Q14.drain, J6.pin1
  N20: Q15.gate, R4.Pin_0
  N21: Q15.drain, J6.pin2
  N22: Q16.gate, R6.Pin_0
  N23: Q16.drain, J6.pin3
  N24: Q17.gate, R8.Pin_0
  N25: Q17.drain, J6.pin4
  N26: Q18.gate, R10.Pin_0
  N27: Q18.drain, J6.pin5
  N28: Q19.gate, R14.Pin_0
  N29: Q19.drain, J6.pin7
  N30: Q20.gate, R12.Pin_0
  N31: Q20.drain, J6.pin6
  N32: Q21.gate, R16.Pin_0
  N33: Q21.drain, J6.pin8
  N34: Part2.D11_PWM/MOSI, J7.pin8, J8.pin8
  N35: Part2.D13/SCK, J7.pin7, J8.pin7
  GND: Part2.GND, J1.GND, J7.pin1, J8.pin1
  N36: Part2.D2, J7.pin6
  N37: Part2.D3_PWM, J8.pin6
  N38: Part2.D6_PWM, J7.pin5
  N39: Part2.D7, J8.pin5
  N40: Part2.5V, J8.pin2

notes:
  Display LED power input. +5V-DC, 500mA max.
  Display Connector #1
  Display Connector #2
  Display Connector #3
